// Logisim project UART_Controller.circ as structural Verilog: 2 circuits, main circuit uart
module uart (
  input  clock,
  input  I_Osel,
  input  rd_wr,
  input  [15:0] Idata,
  input  [7:0] I_Oaddr,
  output dt,
  output con,
  output [7:0] Odata
);

  wire and_1_out, and_2_out, and_4_out, uart_1_p7;
  wire [7:0] uart_1_p1, uart_1_p2;

  assign Odata = and_1_out ? uart_1_p1 : 8'bz;  // Controlled_Buffer controlled_buffer_1
  and and_1 (and_1_out, rd_wr, uart_1_p7);
  // UART uart_1: pin names not known; wires that end beside it: uart_1_p1, uart_1_p2, dt, clock, rd_wr, con, uart_1_p7
  and and_2 (and_2_out, ~rd_wr, uart_1_p7);  // AND_Gate
  assign uart_1_p2 = and_2_out ? Idata[7:0] : 8'bz;  // Controlled_Buffer controlled_buffer_2
  and and_3 (uart_1_p7, and_4_out, I_Osel);
  and and_4 (and_4_out, ~I_Oaddr[7], I_Oaddr[6], I_Oaddr[5], I_Oaddr[4], I_Oaddr[3], I_Oaddr[2], ~I_Oaddr[1], ~I_Oaddr[0]);  // AND_Gate

  // Notes on the sheet:
  //   To interrupt arbiter
endmodule

module IntArb (
  input  clock,
  input  IAck,
  input  [1:0] status,
  input  dt,
  input  con,
  output IRQ,
  output [5:0] vec
);

  wire and_1_out, and_2_out, and_3_out, and_4_out, nand_1_out, not_1_out, not_2_out, or_1_out;
  wire [5:0] and_5_out, and_6_out, or_2_out;
  wire [5:5] Connection_q, DataAvail_q;

  not not_1 (not_1_out, dt);
  and and_1 (and_1_out, not_1_out, dt);
  not not_2 (not_2_out, con);
  and and_2 (and_2_out, not_2_out, con);
  nand nand_1 (nand_1_out, status[0], ~status[1]);  // NAND_Gate
  assign vec = and_4_out ? or_2_out : 6'bz;  // Controlled_Buffer controlled_buffer_1
  and and_3 (and_3_out, IAck, nand_1_out);
  and and_4 (and_4_out, IRQ, and_3_out);
  or or_1 (or_1_out, and_2_out, and_1_out);
  S_R_Flip_Flop #(.trigger("high")) DataAvail (
    .S(and_1_out), .clk(1'b1), .R(and_2_out), .Q(DataAvail_q[5]));  // open: Qn, preset, reset, en
  S_R_Flip_Flop #(.trigger("high")) Connection (
    .S(and_2_out), .clk(1'b1), .R(and_1_out), .Q(Connection_q[5]));  // open: Qn, preset, reset, en
  assign and_5_out = {6{DataAvail_q[5]}} & 6'b010001;  // AND_Gate and_5, 6 bits wide
  assign and_6_out = {6{Connection_q[5]}} & 6'b010000;  // AND_Gate and_6, 6 bits wide
  assign or_2_out = and_5_out | and_6_out;  // OR_Gate or_2, 6 bits wide
  S_R_Flip_Flop #(.trigger("falling")) s_r_ff_1 (
    .S(1'b0), .clk(clock), .R(and_3_out), .Q(IRQ), .preset(or_1_out));  // open: Qn, reset, en
endmodule
