// Logisim project main.circ as structural Verilog: 1 circuit, main circuit main
module main (
);

  wire and_1_out, and_4_out, and_5_out, and_6_out, and_7_out, and_8_out, and_9_out, and_10_out, cdm_16_1_p4,
       cdm_16_1_p5, cdm_16_1_p7, cdm_16_1_p8, cdm_16_1_p10, cdm_16_1_p11, clock, con, dt, HS, I_Osel, IAck,
       in_out_prime, IRQ, main_2_iack_2, main_2_iack_3, main_3_iack_3, main_3_irq_3, mem, not_1_out,
       not_2_out, not_3_out, not_4_out, not_5_out, or_1_out, or_2_out, RAM, s_r_ff_1_q, s_r_ff_2_q,
       s_r_ff_3_qn, word;
  wire [1:0] status;
  wire [5:0] vec;
  wire [15:0] adr, cdm_16_1_p16, cdm_16_1_p17, data;
  wire [31:0] main_1_p8, main_1_p9, main_1_p10, main_1_p11, main_1_p12, main_1_p13, main_1_p14, main_1_p15,
       main_1_p16, main_1_p17, main_1_p18, main_1_p19, main_1_p20, main_1_p21, main_1_p22, main_1_p23,
       main_1_p24, main_1_p25, main_1_p26, main_1_p27, main_1_p28, main_1_p29, main_1_p30, main_1_p31,
       main_1_p32, main_1_p33, main_1_p34, main_1_p35, main_1_p36, main_1_p37, main_1_p38, main_1_p39;

  // Probe on cdm_16_1_p4
  // Probe on cdm_16_1_p5
  // CdM_16 cdm_16_1: pin names not known; wires that end beside it: IRQ, vec, IAck, cdm_16_1_p4, cdm_16_1_p5, clock, cdm_16_1_p7, cdm_16_1_p8, status, cdm_16_1_p10, cdm_16_1_p11, mem, in_out_prime, word, adr, cdm_16_1_p16, cdm_16_1_p17
  Clock clock_1 (.out(clock));
  Button Hard_reset (.out(HS));
  // Probe on cdm_16_1_p7
  // Probe on cdm_16_1_p8
  // Probe on status
  // Probe on cdm_16_1_p10
  // Probe on cdm_16_1_p11
  // Probe on adr
  assign data = not_1_out ? cdm_16_1_p16 : 16'bz;  // Controlled_Buffer controlled_buffer_1
  not not_1 (not_1_out, in_out_prime);
  assign cdm_16_1_p17 = in_out_prime ? data : 16'bz;  // Controlled_Buffer controlled_buffer_2
  // ExpMatrixcontroller_main main_1: pin names not known; wires that end beside it: data, in_out_prime, adr[7:0], I_Osel, data, clock, HS, main_1_p8, main_1_p9, main_1_p10, main_1_p11, main_1_p12, main_1_p13, main_1_p14, main_1_p15, main_1_p16, main_1_p17, main_1_p18, main_1_p19, main_1_p20, main_1_p21, main_1_p22, main_1_p23, main_1_p24, main_1_p25, main_1_p26, main_1_p27, main_1_p28, main_1_p29, main_1_p30, main_1_p31, main_1_p32, main_1_p33, main_1_p34, main_1_p35, main_1_p36, main_1_p37, main_1_p38, main_1_p39
  DotMatrix #(.inputtype("row"), .matrixcols(32), .matrixrows(32)) dotmatrix_1 (
    .row0(main_1_p8), .row1(main_1_p9), .row2(main_1_p10), .row3(main_1_p11), .row4(main_1_p12),
    .row5(main_1_p13), .row6(main_1_p14), .row7(main_1_p15), .row8(main_1_p16), .row9(main_1_p17),
    .row10(main_1_p18), .row11(main_1_p19), .row12(main_1_p20), .row13(main_1_p21), .row14(main_1_p22),
    .row15(main_1_p23), .row16(main_1_p24), .row17(main_1_p25), .row18(main_1_p26), .row19(main_1_p27),
    .row20(main_1_p28), .row21(main_1_p29), .row22(main_1_p30), .row23(main_1_p31), .row24(main_1_p32),
    .row25(main_1_p33), .row26(main_1_p34), .row27(main_1_p35), .row28(main_1_p36), .row29(main_1_p37),
    .row30(main_1_p38), .row31(main_1_p39));
  // RAM ram_1: pin names not known; wires that end beside it: adr, word, RAM, clock, in_out_prime, data
  // Probe on data
  and and_1 (and_1_out, adr[8], adr[9], adr[10], adr[11], adr[12], adr[13], adr[14], adr[15]);
  Pull_Resistor pull_resistor_1 (.node(data[8]));
  Pull_Resistor pull_resistor_2 (.node(data[9]));
  Pull_Resistor pull_resistor_3 (.node(data[10]));
  Pull_Resistor pull_resistor_4 (.node(data[11]));
  Pull_Resistor pull_resistor_5 (.node(data[12]));
  Pull_Resistor pull_resistor_6 (.node(data[13]));
  Pull_Resistor pull_resistor_7 (.node(data[14]));
  Pull_Resistor pull_resistor_8 (.node(data[15]));
  and and_2 (RAM, ~and_1_out, mem);  // AND_Gate
  and and_3 (I_Osel, mem, and_1_out);
  uart uart_1 (
    .Odata(data[7:0]), .Idata(data), .I_Oaddr(adr[7:0]), .I_Osel(I_Osel), .dt(dt), .con(con), .clock(clock),
    .rd_wr(in_out_prime));
  or or_1 (or_1_out, HS, and_5_out);
  and and_4 (and_4_out, con, not_3_out);
  and and_5 (and_5_out, not_2_out, main_2_iack_3);
  not not_2 (not_2_out, main_2_iack_3);
  not not_3 (not_3_out, con);
  IntArbiter_main main_2 (
    .IAck_3(main_2_iack_3), .vec(6'b010000), .IRQ_2(s_r_ff_1_q), .IAck(IAck), .Rset(HS),
    .IAck_2(main_2_iack_2), .vecbus(vec), .IRQ(main_3_irq_3), .IRQ_3(IRQ), .status(status), .clock(clock));
  S_R_Flip_Flop #(.trigger("high")) s_r_ff_1 (
    .S(and_4_out), .clk(1'b1), .R(or_1_out), .Q(s_r_ff_1_q));  // open: Qn, preset, reset, en
  and and_6 (and_6_out, not_4_out, and_7_out);
  not not_4 (not_4_out, and_7_out);
  or or_2 (or_2_out, HS, and_10_out);
  and and_7 (and_7_out, dt, s_r_ff_3_qn);
  and and_8 (and_8_out, and_9_out, I_Osel);
  and and_9 (and_9_out, ~adr[7], adr[6], adr[5], adr[4], adr[3], ~adr[2], ~adr[1], ~adr[0]);  // AND_Gate
  IntArbiter_main main_3 (
    .IAck_3(main_3_iack_3), .vec(6'b010001), .IRQ_2(s_r_ff_2_q), .IAck(main_2_iack_2), .Rset(HS),
    .vecbus(vec), .IRQ(1'b0), .IRQ_3(main_3_irq_3), .status(status), .clock(clock));  // open: IAck_2
  S_R_Flip_Flop #(.trigger("high")) s_r_ff_2 (
    .S(and_6_out), .clk(1'b1), .R(or_2_out), .Q(s_r_ff_2_q));  // open: Qn, preset, reset, en
  not not_5 (not_5_out, main_3_iack_3);
  and and_10 (and_10_out, not_5_out, main_3_iack_3);
  S_R_Flip_Flop #(.trigger("high")) s_r_ff_3 (
    .S(and_10_out), .clk(1'b1), .R(and_8_out), .Qn(s_r_ff_3_qn));  // open: Q, preset, reset, en

  // Other names for the same wires on the sheet: I_Odat[15:0] = data; I_Oaddr[7:0] = adr[7:0];
  //   rd_wr_prime = in_out_prime

  // Notes on the sheet:
  //   UART
endmodule
